// Digital circuit CC.dig as structural Verilog
module CC (
  input  [6:0] OPCODE
);

  wire and_1_out, and_2_out, and_4_out, not_1_out, not_2_out, not_3_out;

  not not_1 (not_1_out, OPCODE[0]);
  and and_1 (and_1_out, OPCODE[1], not_1_out);
  not not_2 (not_2_out, OPCODE[3]);
  and and_2 (and_2_out, not_2_out, OPCODE[2]);
  // And and_3 has open pins: In_1=and_4_out, In_2=and_2_out, In_3=and_1_out, out=open
  not not_3 (not_3_out, OPCODE[4]);
  and and_4 (and_4_out, OPCODE[6], OPCODE[5], not_3_out);
endmodule
