// Digital circuit ProjetoMicroarquitetural.dig as structural Verilog
module ProjetoMicroarquitetural (
  input  clk
);

  wire brg_1_p4, brg_1_p10, brg_1_p11, brg_1_p12, multiplexer_2_out, PC_p1, ula_1_p1, ula_1_p2, ula_1_p6,
       ula_1_p8, ula_1_p9;
  wire [1:0] PC_p2, ula_1_p10;
  wire [19:0] brg_1_p1;
  wire [31:0] add_1_p3, immext_1_s, MDD_d, MI_d, ula_1_p7;
  wire [31:1] undriven;

  // REG PC: pin names not known; wires that end beside it: PC_p1, PC_p2
  // Not not_1 has open pins: in=clk, out=open
  // ADD add_1: pin names not known; wires that end beside it: PC_p1, PC_p2, add_1_p3, {MI_d[31:27], brg_1_p1[19:18]}
  ROM #(.isProgramMemory("true")) MI (.A(PC_p2), .sel(1'b1), .D(MI_d[0]));
  Multiplexer #(.Selector_Bits(2), .Bits(32)) multiplexer_1 (
    .in_0({undriven, 1'b0}), .in_1(32'h4), .in_2(ula_1_p7), .in_3(immext_1_s), .out(add_1_p3));  // open: sel
  CC cc_1 (.OPCODE(MI_d[6:0]));
  IMMEXT immext_1 (.E(brg_1_p1), .S(immext_1_s));  // open: TPIMM
  // BRG brg_1: pin names not known; wires that end beside it: brg_1_p1[4:0], {MI_d[31:27], brg_1_p1[19:18]}, brg_1_p1[7:5], brg_1_p4, brg_1_p1[12:8], brg_1_p1[17:13], brg_1_p1[4:0], brg_1_p4, clk, brg_1_p10, brg_1_p11, brg_1_p12
  Multiplexer multiplexer_2 (.sel(ula_1_p1), .in_0(brg_1_p12), .in_1(immext_1_s[0]), .out(multiplexer_2_out));
  // ULA ula_1: pin names not known; wires that end beside it: ula_1_p1, ula_1_p2, brg_1_p11, multiplexer_2_out, ula_1_p2, ula_1_p6, ula_1_p7, ula_1_p8, ula_1_p9, ula_1_p10
  LED led_1 (.in(ula_1_p6));
  Multiplexer #(.Selector_Bits(2)) multiplexer_3 (
    .sel(ula_1_p10), .in_0(1'b0), .in_1(PC_p2[0]), .in_2(MDD_d[0]), .in_3(ula_1_p7[0]), .out(brg_1_p10));
  RAMDualPort #(.AddrBits(5), .Bits(32)) MDD (
    .Din(ula_1_p7), .str(ula_1_p9), .C(clk), .ld(ula_1_p8), .D(MDD_d));  // open: A
  // Pins of 1 and 32 bits meet at ula_1_p7
  // Pins of 1 and 32 bits meet at MDD_d
  // Pins of 1 and 2 bits meet at PC_p2
  // Pins of 1 and 32 bits meet at {MI_d[31:27], brg_1_p1, MI_d[6:0]}
  // Pins of 1 and 32 bits meet at {undriven, 1'b0}
  // Pins of 1 and 32 bits meet at immext_1_s
endmodule
